// Digital circuit ULAprincipal.dig as structural Verilog
module ULAprincipal (
  input  nInversor,
  input  Carry,
  input  Sub,
  input  [7:0] A,
  input  [7:0] B,
  output C_out,
  output Flg_Z
);

  wire or_1_out, sapula0_1_p7, sapula0_2_p7, sapula0_3_p7, sapula0_4_p7, sapula0_5_p7, sapula0_6_p7,
       sapula0_7_p7;
  wire [3:0] sapula0_1_p6, sapula0_5_p6;

  or or_1 (or_1_out, Carry, Sub);
  // sapULA0 sapula0_1: pin names not known; wires that end beside it: or_1_out, A[0], nInversor, B[0], Sub, sapula0_1_p6[0], sapula0_1_p7
  // sapULA0 sapula0_2: pin names not known; wires that end beside it: sapula0_1_p7, A[1], nInversor, B[1], Sub, sapula0_1_p6[1], sapula0_2_p7
  // sapULA0 sapula0_3: pin names not known; wires that end beside it: sapula0_2_p7, A[2], nInversor, B[2], Sub, sapula0_1_p6[2], sapula0_3_p7
  // sapULA0 sapula0_4: pin names not known; wires that end beside it: sapula0_3_p7, A[3], nInversor, B[3], Sub, sapula0_1_p6[3], sapula0_4_p7
  // sapULA0 sapula0_5: pin names not known; wires that end beside it: sapula0_4_p7, A[4], nInversor, B[4], Sub, sapula0_5_p6[0], sapula0_5_p7
  // sapULA0 sapula0_6: pin names not known; wires that end beside it: sapula0_5_p7, A[5], nInversor, B[5], Sub, sapula0_5_p6[1], sapula0_6_p7
  // sapULA0 sapula0_7: pin names not known; wires that end beside it: sapula0_6_p7, A[6], nInversor, B[6], Sub, sapula0_5_p6[2], sapula0_7_p7
  // sapULA0 sapula0_8: pin names not known; wires that end beside it: sapula0_7_p7, A[7], nInversor, B[7], Sub, sapula0_5_p6[3], C_out
  Seven_Seg_Hex seven_seg_hex_1 (.d(A[7:4]), .dp(1'b0));
  Seven_Seg_Hex seven_seg_hex_2 (.d(sapula0_5_p6), .dp(1'b0));
  Seven_Seg_Hex seven_seg_hex_3 (.d(A[3:0]), .dp(1'b0));
  Seven_Seg_Hex seven_seg_hex_4 (.d(sapula0_1_p6), .dp(1'b0));
  Seven_Seg_Hex seven_seg_hex_5 (.d(B[7:4]), .dp(1'b0));
  nand nand_1 (Flg_Z, sapula0_1_p6[0], sapula0_1_p6[1], sapula0_1_p6[2], sapula0_1_p6[3], sapula0_5_p6[0], sapula0_5_p6[1], sapula0_5_p6[2], sapula0_5_p6[3]);
  Seven_Seg_Hex seven_seg_hex_6 (.d(B[3:0]), .dp(1'b0));

  // Other names for the same wires on the sheet: RA[7:0] = A; RB[7:0] = B

  // Notes on the sheet:
  //   nInversor: default 1
endmodule
