// Digital circuit andOr.dig as structural Verilog
module andOr (
  input  _1,
  input  _0,
  input  _1_2,
  input  _0_2,
  output out_5
);

  wire and_1_out, and_2_out;

  and and_1 (and_1_out, _1, _0);
  and and_2 (and_2_out, _1_2, _0_2);
  or or_1 (out_5, and_1_out, and_2_out);
endmodule
