// Digital circuit base.dig as structural Verilog
module base (
);

  wire dipswitch_1_out, dipswitch_2_out, dipswitch_3_out, dipswitch_4_out, dipswitch_5_out, dipswitch_6_out,
       dipswitch_7_out, dipswitch_8_out, dipswitch_9_out, dipswitch_10_out;
  wire [3:0] regis8bits_1_q, regis8bits_1_q_5;

  DipSwitch dipswitch_1 (.out(dipswitch_1_out));
  DipSwitch dipswitch_2 (.out(dipswitch_2_out));
  DipSwitch dipswitch_3 (.out(dipswitch_3_out));
  DipSwitch dipswitch_4 (.out(dipswitch_4_out));
  DipSwitch dipswitch_5 (.out(dipswitch_5_out));
  DipSwitch dipswitch_6 (.out(dipswitch_6_out));
  DipSwitch dipswitch_7 (.out(dipswitch_7_out));
  DipSwitch dipswitch_8 (.out(dipswitch_8_out));
  DipSwitch dipswitch_9 (.out(dipswitch_9_out));
  DipSwitch dipswitch_10 (.out(dipswitch_10_out));
  regis8bits regis8bits_1 (
    .D(dipswitch_1_out), .ENA_i(dipswitch_9_out), .D_2(dipswitch_2_out), .D_3(dipswitch_3_out),
    .D_4(dipswitch_4_out), .D_5(dipswitch_5_out), .D_6(dipswitch_6_out), .D_7(dipswitch_7_out),
    .D_8(dipswitch_8_out), .ENA_o(dipswitch_10_out), .Q(regis8bits_1_q[0]), .Q_2(regis8bits_1_q[1]),
    .Q_3(regis8bits_1_q[2]), .Q_4(regis8bits_1_q[3]), .Q_5(regis8bits_1_q_5[0]), .Q_6(regis8bits_1_q_5[1]),
    .Q_7(regis8bits_1_q_5[2]), .Q_8(regis8bits_1_q_5[3]));
  Seven_Seg_Hex seven_seg_hex_1 (.d(regis8bits_1_q), .dp(1'b0));
  Seven_Seg_Hex seven_seg_hex_2 (.d(regis8bits_1_q_5), .dp(1'b0));
endmodule
