// Digital circuit ffRS.dig as structural Verilog
module ffRS (
  output Si,
  output Ri,
  output Si_2,
  output Ri_2,
  output Si_3,
  output Ri_3,
  output Si_4,
  output Ri_4
);

  wire dipswitch_1_out, dipswitch_2_out, dipswitch_3_out, dipswitch_4_out, dipswitch_5_out, nand_1_out,
       nand_2_out, nand_3_out, nand_4_out, nand_5_out, nand_6_out, nand_7_out, nand_8_out, not_1_out,
       not_2_out, not_3_out, not_4_out;

  DipSwitch dipswitch_1 (.out(dipswitch_1_out));
  DipSwitch dipswitch_2 (.out(dipswitch_2_out));
  DipSwitch dipswitch_3 (.out(dipswitch_3_out));
  DipSwitch dipswitch_4 (.out(dipswitch_4_out));
  DipSwitch dipswitch_5 (.out(dipswitch_5_out));
  not not_1 (not_1_out, dipswitch_1_out);
  not not_2 (not_2_out, dipswitch_2_out);
  not not_3 (not_3_out, dipswitch_3_out);
  not not_4 (not_4_out, dipswitch_4_out);
  and and_1 (Si, dipswitch_1_out, dipswitch_5_out);
  and and_2 (Ri, not_1_out, dipswitch_5_out);
  and and_3 (Si_2, dipswitch_2_out, dipswitch_5_out);
  and and_4 (Ri_2, not_2_out, dipswitch_5_out);
  and and_5 (Si_3, dipswitch_3_out, dipswitch_5_out);
  and and_6 (Ri_3, not_3_out, dipswitch_5_out);
  and and_7 (Si_4, dipswitch_4_out, dipswitch_5_out);
  and and_8 (Ri_4, not_4_out, dipswitch_5_out);
  nand nand_1 (nand_1_out, Si, nand_2_out);
  nand nand_2 (nand_2_out, nand_1_out, Ri);
  nand nand_3 (nand_3_out, Si_2, nand_4_out);
  nand nand_4 (nand_4_out, nand_3_out, Ri_2);
  nand nand_5 (nand_5_out, Si_3, nand_6_out);
  nand nand_6 (nand_6_out, nand_5_out, Ri_3);
  nand nand_7 (nand_7_out, Si_4, nand_8_out);
  nand nand_8 (nand_8_out, nand_7_out, Ri_4);
  LED S (.in(nand_1_out));
  LED R (.in(nand_2_out));
  LED S_2 (.in(nand_3_out));
  LED R_2 (.in(nand_4_out));
  LED S_3 (.in(nand_5_out));
  LED R_3 (.in(nand_6_out));
  LED S_4 (.in(nand_7_out));
  LED R_4 (.in(nand_8_out));
endmodule
