// Digital circuit flip_flop_jk.dig as structural Verilog
module flip_flop_jk (
  input  clk,
  input  J,
  input  K,
  output Q,
  output Q_2
);

  wire nand_1_out, nand_2_out;

  nand nand_1 (nand_1_out, Q_2, clk);
  nand nand_2 (nand_2_out, clk, Q);
  not nand_3 (Q, Q_2);  // NAnd open: In_1
  not nand_4 (Q_2, Q);  // NAnd open: In_2
endmodule
