// Digital circuit ldcount.dig as structural Verilog
module ldcount (
  input  Clear,
  input  CCount_e,
  input  ncnt__LD,
  input  Cascade,
  input  Clock,
  input  D0,
  output Q,
  output nQ
);

  wire and_1_out, and_2_out, and_3_out, not_1_out, not_2_out, or_1_out;

  not not_1 (not_1_out, D0);
  not not_2 (not_2_out, ncnt__LD);
  and and_1 (and_1_out, not_1_out, ncnt__LD);
  and and_2 (and_2_out, D0, ncnt__LD);
  and and_3 (and_3_out, CCount_e, Cascade, not_2_out);
  or or_1 (or_1_out, and_1_out, Clear);
  JK_FF_AS jk_ff_as_1 (.Set(and_2_out), .J(and_3_out), .C(Clock), .K(and_3_out), .Clr(or_1_out), .Q(Q), .nQ(nQ));

  // Notes on the sheet:
  //   CCount_e: default 1
  //   Cascade: default 1
endmodule
