// Digital circuit pc3.dig as structural Verilog
module pc3 (
  input  clk,
  input  in_2,
  input  ncnt_LD,
  input  Clear,
  input  Count_E,
  input  in_6,
  input  in_7,
  input  in_8,
  input  in_9,
  input  in_10
);

  wire and_1_out, and_2_out, and_3_out, dipswitch_1_out, ldcount_1_q, ldcount_2_q, ldcount_3_q, ldcount_4_q,
       ldcount_5_q;
  wire [1:0] counter_1_out;

  DipSwitch dipswitch_1 (.out(dipswitch_1_out));
  Counter #(.Bits(2), .isProgramCounter("true")) counter_1 (
    .en(in_2), .C(clk), .clr(dipswitch_1_out), .out(counter_1_out));  // open: ovf
  LED led_1 (.in(counter_1_out[0]));
  LED led_2 (.in(counter_1_out[1]));
  ldcount ldcount_1 (
    .Clear(Clear), .CCount_e(Count_E), .ncnt__LD(ncnt_LD), .Cascade(1'b1), .Clock(counter_1_out[1]),
    .D0(in_6), .Q(ldcount_1_q));  // open: nQ
  LED led_3 (.in(ldcount_1_q));
  ldcount ldcount_2 (
    .Clear(Clear), .CCount_e(Count_E), .ncnt__LD(ncnt_LD), .Cascade(ldcount_1_q), .Clock(counter_1_out[1]),
    .D0(in_7), .Q(ldcount_2_q));  // open: nQ
  and and_1 (and_1_out, ldcount_2_q, ldcount_1_q);
  LED led_4 (.in(ldcount_2_q));
  ldcount ldcount_3 (
    .Clear(Clear), .CCount_e(Count_E), .ncnt__LD(ncnt_LD), .Cascade(and_1_out), .Clock(counter_1_out[1]),
    .D0(in_8), .Q(ldcount_3_q));  // open: nQ
  and and_2 (and_2_out, ldcount_3_q, and_1_out);
  LED led_5 (.in(ldcount_3_q));
  ldcount ldcount_4 (
    .Clear(Clear), .CCount_e(Count_E), .ncnt__LD(ncnt_LD), .Cascade(and_2_out), .Clock(counter_1_out[1]),
    .D0(in_9), .Q(ldcount_4_q));  // open: nQ
  and and_3 (and_3_out, ldcount_4_q, and_2_out);
  LED led_6 (.in(ldcount_4_q));
  ldcount ldcount_5 (
    .Clear(Clear), .CCount_e(Count_E), .ncnt__LD(ncnt_LD), .Cascade(and_3_out), .Clock(counter_1_out[1]),
    .D0(in_10), .Q(ldcount_5_q));  // open: nQ
  LED led_7 (.in(ldcount_5_q));

  // Notes on the sheet:
  //   clk: Hz: 5
  //   in_2: default 1
endmodule
