// Digital circuit pc5bits.dig as structural Verilog
module pc5bits (
  input  Re_a,
  input  Le_a,
  input  Counte_a,
  input  Clock,
  input  Clear,
  input  [7:0] PC_in,
  input  A0_2,
  input  A1_2,
  input  A2_2,
  input  A3_2,
  input  A4_2,
  output A0,
  output A1,
  output A2,
  output A3,
  output A4,
  output [7:0] PC_out
);

  wire A0_d, and_1_out, and_2_out, and_3_out, and_4_out, and_5_out, and_6_out, and_7_out, and_8_out,
       and_9_out, jk_ff_as_2_q, jk_ff_as_3_q, jk_ff_as_4_q, jk_ff_as_5_q;

  and and_1 (and_1_out, A0_2, Le_a);
  and and_2 (and_2_out, Counte_a, A0_d);
  JK_FF_AS jk_ff_as_1 (.Set(and_1_out), .J(Counte_a), .C(Clock), .K(Counte_a), .Clr(Clear), .Q(A0_d));  // open: nQ
  assign A0 = Re_a ? A0_d : 1'bz;  // Driver driver_1
  and and_3 (and_3_out, A1_2, Le_a);
  JK_FF_AS jk_ff_as_2 (
    .Set(and_3_out), .J(and_2_out), .C(Clock), .K(and_2_out), .Clr(Clear), .Q(jk_ff_as_2_q));  // open: nQ
  assign A1 = Re_a ? jk_ff_as_2_q : 1'bz;  // Driver driver_2
  and and_4 (and_4_out, A2_2, Le_a);
  and and_5 (and_5_out, Counte_a, jk_ff_as_2_q);
  JK_FF_AS jk_ff_as_3 (
    .Set(and_4_out), .J(and_5_out), .C(Clock), .K(and_5_out), .Clr(Clear), .Q(jk_ff_as_3_q));  // open: nQ
  assign A2 = Re_a ? jk_ff_as_3_q : 1'bz;  // Driver driver_3
  and and_6 (and_6_out, Counte_a, jk_ff_as_3_q);
  and and_7 (and_7_out, A3_2, Le_a);
  JK_FF_AS jk_ff_as_4 (
    .Set(and_7_out), .J(and_6_out), .C(Clock), .K(and_6_out), .Clr(Clear), .Q(jk_ff_as_4_q));  // open: nQ
  assign A3 = Re_a ? jk_ff_as_4_q : 1'bz;  // Driver driver_4
  and and_8 (and_8_out, A4_2, Le_a);
  and and_9 (and_9_out, Counte_a, jk_ff_as_4_q);
  assign A4 = Re_a ? jk_ff_as_5_q : 1'bz;  // Driver driver_5
  JK_FF_AS jk_ff_as_5 (
    .Set(and_8_out), .J(and_9_out), .C(Clock), .K(and_9_out), .Clr(Clear), .Q(jk_ff_as_5_q));  // open: nQ
  PullDown #(.Bits(3)) pulldown_1 (.out(PC_out[7:5]));
  // Pins of 1 and 8 bits meet at {PC_out[7:5], A4, A3, A2, A1, A0}
  // Pins of 1 and 8 bits meet at {PC_in[7:5], A4_2, A3_2, A2_2, A1_2, A0_2}

  assign PC_in[4:0] = {A4_2, A3_2, A2_2, A1_2, A0_2};
  assign PC_out[4:0] = {A4, A3, A2, A1, A0};
endmodule
