// Digital circuit regisMainBus.dig as structural Verilog
module regisMainBus (
  input  E_in,
  input  [7:0] D_x,
  input  E_out,
  output [7:0] Q_x
);

  Flip_Flop_tipo_D flip_flop_tipo_d_1 (.D(D_x[0]), .E_in(E_in), .Q(Q_x[0]), .E_out(E_out));
  Flip_Flop_tipo_D flip_flop_tipo_d_2 (.D(D_x[1]), .E_in(E_in), .Q(Q_x[1]), .E_out(E_out));
  // Flip_Flop_tipo_D flip_flop_tipo_d_3: pin names not known; wires that end beside it: D_x[2], E_in, E_out, Q_x[2], Q_x[3]
  Flip_Flop_tipo_D flip_flop_tipo_d_4 (.D(D_x[3]), .E_in(E_in), .Q(Q_x[3]), .E_out(E_out));
  Flip_Flop_tipo_D flip_flop_tipo_d_5 (.D(D_x[4]), .E_in(E_in), .Q(Q_x[4]), .E_out(E_out));
  Flip_Flop_tipo_D flip_flop_tipo_d_6 (.D(D_x[5]), .E_in(E_in), .Q(Q_x[5]), .E_out(E_out));
  Flip_Flop_tipo_D flip_flop_tipo_d_7 (.D(D_x[6]), .E_in(E_in), .Q(Q_x[6]), .E_out(E_out));
  Flip_Flop_tipo_D flip_flop_tipo_d_8 (.D(D_x[7]), .E_in(E_in), .Q(Q_x[7]), .E_out(E_out));
endmodule
