// Digital circuit sap1Contro.dig as structural Verilog
module sap1Contro (
  input  Cp,
  input  Ep,
  input  nLm,
  input  nCe,
  input  nL1,
  input  nE1,
  input  nLa,
  input  Ea,
  input  Su,
  input  Eu,
  input  nLb,
  input  nLo
);
endmodule
