// Digital circuit sapULA0.dig as structural Verilog
module sapULA0 (
  input  CY_in,
  input  A,
  input  B,
  input  SUB,
  input  nINV,
  output S,
  output CY_ou
);

  wire and_1_out, and_2_out, and_3_out, and_4_out, not_1_out, xor_1_out, xor_2_out, xor_3_out;

  xor xor_1 (xor_1_out, B, SUB);
  and and_1 (and_1_out, CY_in, nINV);
  not not_1 (not_1_out, nINV);
  xor xor_2 (xor_2_out, A, not_1_out);
  and and_2 (and_2_out, nINV, xor_1_out);
  xor xor_3 (xor_3_out, xor_2_out, and_2_out);
  and and_3 (and_3_out, xor_2_out, and_2_out);
  xor xor_4 (S, and_1_out, xor_3_out);
  and and_4 (and_4_out, and_1_out, xor_3_out);
  or or_1 (CY_ou, and_4_out, and_3_out);
endmodule
